# Fritzing sketch IRRemote (saved by Fritzing 0.9.3b)
breadboards: 1

parts:
  S1 = Pushbutton [package="[THT]"]
  R1 = Resistor [tolerance=±5% resistance=1k package=THT]
  R2 = Resistor [tolerance=±5% resistance=10k package=THT]
  Q1 = NPN-Transistor [part_number=2N2222A package="TO92 [THT]"]
  U1 = ESP8266-12 [part_number=ESP8266-12e]
  LED1 = LED - 5mm [color="Infrared (940nm)" current=0.1A package="5 mm [THT]"]
  U2 = Voltage Regulator - 3.3V [package="TO220 [THT]"]
  R4 = Resistor [tolerance=±5% resistance=10k package=THT]
  R5 = Resistor [tolerance=±5% resistance=1k package=THT]
  C1 = Ceramic Capacitor [capacitance=100nF package="100 mil [THT, multilayer]"]
  C2 = Ceramic Capacitor [capacitance=10µF package="100 mil [THT, multilayer]"]
  R3 = Resistor [tolerance=±5% resistance=10 package=THT]
  LED2 = LED - 3mm [color="Red (633nm)" current=20mA package="3 mm [THT]"]
  R6 = Resistor [tolerance=±5% resistance=220 package=THT]

nets:
  N1: S1.Pin_1, S1.Pin_2, R4.Pin_1, R5.Pin_0
  GND: S1.Pin_3, S1.Pin_4, Q1.C, U1.GND, U2.GND, C1.0, C2.0
  N2: R1.Pin_0, R2.Pin_0, U1.GPIO4
  N3: R1.Pin_1, Q1.B
  N4: R2.Pin_1, U1.VCC, U2.output_voltage, R4.Pin_0, C2.1, R3.Pin_1, LED2.cathode
  N5: Q1.E, LED1.anode
  N6: U1.GPIO14, R5.Pin_1
  N7: U1.GPIO12, R6.Pin_1
  N8: LED1.cathode, R3.Pin_0
  5V: U2.input_voltage, C1.1
  N9: LED2.anode, R6.Pin_0
